# Fritzing sketch Breadboard Diagram (saved by Fritzing 1.0.2b)
breadboards: 1

parts:
  Part1 = Arduino Uno (Rev3)
  U1 = LCD-16X2 [package=lcd-16x2_noholes]
  POT1 = Breadboard Trimpot
  POT2 = Breadboard Trimpot
  J1 = Basic Servo

nets:
  N1: Part1.A0, POT2.PIN2
  N2: Part1.D8, U1.DB7
  N3: Part1.D9_PWM, U1.DB6
  N4: Part1.D10_PWM/SS, U1.DB5
  N5: Part1.D11_PWM/MOSI, U1.DB4
  N6: Part1.D12/MISO, U1.E
  N7: Part1.D13/SCK, U1.RS
  N8: Part1.D3_PWM, J1.pulse
  5V: Part1.5V, U1.VDD, U1.A, POT1.PIN1, POT2.PIN1, J1.vcc
  GND: Part1.GND, U1.VSS, U1.R_W, U1.K, POT1.PIN3, POT2.PIN3, J1.gnd
  N9: U1.VO, POT1.PIN2
